# Fritzing sketch Devre-sema (saved by Fritzing 0.9.3b)
circuit board: 8.46667cm x 5.64444cm
breadboards: 1

parts:
  U1 = GAS_SENSOR [package=mq-3]
  Raspberry_Pi1 = Raspberry Pi B+
  ADC1 = MCP3008 [package=dil16]
  Parça1 = IFR520 MOS module [package=THT]
  M1 = DC Motor

nets:
  N1: U1.A1, ADC1.CH0
  GND: U1.H1, Raspberry_Pi1.GND, ADC1.AGND, Parça1.GND
  5V: U1.H2, Raspberry_Pi1.5V, ADC1.VREF, ADC1.VDD, Parça1.VCC, Parça1.VIN
  N2: Raspberry_Pi1.GPIO22, ADC1.CS/SHDN
  N3: Raspberry_Pi1.GPIO10, ADC1.Din
  N4: Raspberry_Pi1.GPIO9, ADC1.Dout
  N5: Raspberry_Pi1.GPIO11, ADC1.CLK
  N6: Raspberry_Pi1.GPIO18, Parça1.SIG
  N7: Parça1.V+, M1.pin_1
  N8: Parça1.V-, M1.pin_2

notes:
  MQ-2 Sensor Analog Output
  DC Fan
